// Digital circuit Even_parity_generator_&_checker.dig as structural Verilog
module Even_parity_generator___checker (
  input  A,
  input  B,
  input  C,
  input  P_Even_Input,
  output P_even,
  output P_checker_out
);

  wire xor_1_out, xor_3_out, xor_4_out;

  xor xor_1 (xor_1_out, A, B);
  xor xor_2 (P_even, xor_1_out, C);
  xor xor_3 (xor_3_out, A, B);
  xor xor_4 (xor_4_out, P_Even_Input, C);
  xor xor_5 (P_checker_out, xor_3_out, xor_4_out);
endmodule

/* Test case Even_Parity_Generator:
A B C P_even
0 0 0 0
0 0 1 1
0 1 0 1
0 1 1 0
1 0 0 1
1 0 1 0
1 1 0 0
1 1 1 1
*/

/* Test case Odd_Parity_Checker:
A B C P_Even_Input P_checker_out
0 0 0 0            0
0 0 0 1            1
0 0 1 0            1
0 0 1 1            0
0 1 0 0            1
0 1 0 1            0
0 1 1 0            0
0 1 1 1            1
1 0 0 0            1
1 0 0 1            0
1 0 1 0            0
1 0 1 1            1
1 1 0 0            0
1 1 0 1            1
1 1 1 0            1
1 1 1 1            0
*/
