// Digital circuit X_OR - gate.dig as structural Verilog
module X_OR___gate (
  input  A,
  input  B,
  output Y
);

  xor xor_1 (Y, A, B);
  LED led_1 (.in(Y));
endmodule

/* Test case X_OR_Test:
A B Y
0 0 0
0 1 1
1 0 1
1 1 0
*/
